# Fritzing sketch devBoard (saved by Fritzing 0.9.3b)
circuit board: 4.44609cm x 3.35686cm
breadboards: 1

parts:
  U1 = ESP-12F (ESP8266 WiFi Module) [part_number=ESP8266]
  Wake = Schottky Diode [part_number=1N5817 package="300 mil [THT]"]
  RX/TX = female pin header, 2 pins [form="♀ (female)"]
  PRGM = male pin header, 2 pins [form="♂ (male)"]
  R1 = Resistor [tolerance=±5% resistance=10k package=THT]
  R2 = Resistor [tolerance=±5% resistance=10k package=THT]
  R4_7k = Resistor [tolerance=±5% resistance=4.7k package=THT]
  R3 = Resistor [tolerance=±5% resistance=10k package=THT]
  IO = male pin header, 7 pins [form="♂ (male)"]
  Power = female pin header, 2 pins [form="♀ (female)"]
  DS18B20 = female pin header, 3 pins [form="♀ (female)"]
  CConf = male pin header, 2 pins [form="♂ (male)"]

nets:
  N1: U1.RXD0, RX/TX.pin1
  N2: U1.VCC, R1.Pin_0, R2.Pin_0, R4_7k.Pin_0, Power.pin2, DS18B20.pin3
  N3: U1.GPIO0, PRGM.pin1, R2.Pin_1
  N4: U1.GPIO2, R4_7k.Pin_1, DS18B20.pin2
  N5: U1.EN, R1.Pin_1
  N6: U1.GND, PRGM.pin2, R3.Pin_0, Power.pin1, DS18B20.pin1, CConf.pin2
  N7: U1.TXD0, RX/TX.pin2
  N8: U1.GPIO15, R3.Pin_1
  N9: U1.GPIO4, IO.pin1
  N10: U1.GPIO5, IO.pin2
  N11: U1.ADC0, IO.pin7
  N12: U1.GPIO16, Wake.cathode
  N13: U1.GPIO14, CConf.pin1
  N14: U1.GPIO12, IO.pin6
  N15: U1.GPIO13, IO.pin5
  N16: U1.RST, Wake.anode
  N17: U1.GPIO10, IO.pin3
  N18: U1.GPIO9, IO.pin4

notes:
  ADC
  12
  13
  09
  10
  05
  04

custom parts:
  ESP-12F (ESP8266 WiFi Module): WiFi Module based on the ESP8266 with onboard PCB antenna and UART communications
