# Fritzing sketch mount (saved by Fritzing 0.9.3b)
circuit board: 2.50824cm x 2.27787cm
breadboards: 1

parts:
  U1 = ESP-12F (ESP8266 WiFi Module) [part_number=ESP8266]
  DS1 = DS18B20 1-Wire Temperature Sensor [part_number=DS18B20]
  J1 = female pin header, 2 pins [form="♀ (female)"]
  R3 = Resistor [tolerance=±5% resistance=10k package="1206 [SMD]"]
  D1 = Schottky Diode [part_number=1N5817 package="300 mil [THT]"]
  R4 = Resistor [tolerance=±5% resistance=4.7k package="1206 [SMD]"]
  R2 = Resistor [tolerance=±5% resistance=10k package="1206 [SMD]"]
  R1 = Resistor [tolerance=±5% resistance=10k package="1206 [SMD]"]
  S2 = Toggle Switch [package=THT]

nets:
  VCC: U1.VCC, DS1.VDD, J1.pin2, R4.Pin_0, R2.Pin_0, R1.Pin_0
  N1: U1.GPIO0, R2.Pin_1
  N2: U1.GPIO2, DS1.DQ, R4.Pin_1
  N3: U1.EN, R1.Pin_1
  GND: U1.GND, DS1.GND, J1.pin1, R3.Pin_0, S2.COM
  N4: U1.GPIO15, R3.Pin_1
  N5: U1.GPIO16, D1.cathode
  N6: U1.GPIO14, S2.L1
  N7: U1.RST, D1.anode

notes:
  -
  +

custom parts:
  ESP-12F (ESP8266 WiFi Module): WiFi Module based on the ESP8266 with onboard PCB antenna and UART communications
