# Fritzing sketch schematics (saved by Fritzing 0.9.3b)
breadboards: 1

parts:
  U1 = ESP8266-07 [part_number=ESP8266]
  USBTTL1 = USB TTL Serial Cable
  VCC1 = Battery
  R5 = Resistor [tolerance=±5% resistance=10k package=THT]
  D2 = Schottky Diode [part_number=1N5817 package="300 mil [THT]"]
  S3 = Toggle Switch [package=THT]
  S4 = Pushbutton [package=THT]
  R6 = Resistor [tolerance=±5% resistance=10k package=THT]
  R7 = Resistor [tolerance=±5% resistance=10k package=THT]
  R8 = Resistor [tolerance=±5% resistance=10k package=THT]

nets:
  N1: U1.RXD, USBTTL1.TX
  N2: U1.VCC, VCC1.+, S3.L1, R6.Pin_1, R7.Pin_1, R8.Pin_1
  N3: U1.GPIO_0, R8.Pin_0
  N4: U1.CH_PD, R7.Pin_0
  GND: U1.GND, USBTTL1.GND, VCC1.-, R5.Pin_1, S3.COM, S4.leg0
  N5: U1.TXD, USBTTL1.RX
  N6: U1.GPIO_15, R5.Pin_0
  N7: U1.GPIO_16, D2.cathode
  N8: U1.REST, D2.anode, S4.leg1, R6.Pin_0

custom parts:
  ESP8266-07: ESP8266 - 07 WiFi Module on PCB
